# Fritzing sketch fritzing (saved by Fritzing 0.9.0b)
perfboards: 1

parts:
  Part1 = Arduino Pro Mini v13
  NRF24L1 = NRF24L01
  R2 = Resistor [tolerance=±5% resistance=220 package=THT]
  R1 = Resistor [tolerance=±5% resistance=220 package=THT]
  Q3 = Basic FET P-Channel [package="TO220 [THT]"]
  Power_plug1 = Power plug  # not connected
  J+GRB = male pin header, 4 pins [form="♂ (male)"]
  Q1 = Basic FET P-Channel [package="TO220 [THT]"]
  Q2 = Basic FET P-Channel [package="TO220 [THT]"]
  R3 = Resistor [tolerance=±5% resistance=220 package=THT]
  J-12V = male pin header, 2 pins [form="♂ (male)"]
  J-IR = male pin header, 3 pins [form="♂ (male)"]
  J-DS = male pin header, 3 pins [form="♂ (male)"]
  IR1 = TSOP312.., 314.. [part_number=IR package=THT]  # not connected
  R4 = Resistor [tolerance=±5% resistance=4.7k package=THT]
  DS18B20 = DS18B20 1-Wire Temperature Sensor [part_number=DS18B20]  # not connected
  J-LDR = male pin header, 2 pins [form="♂ (male)"]
  LDR = Photocell (LDR) [package=THT]  # not connected
  R5 = Resistor [tolerance=±5% resistance=10k package=THT]
  L-IR = LED - 5mm [color="Red (633nm)" package="5 mm [THT]"]
  L-RGB = RGB LED (com. cathode, rgb) [package="5 mm [THT]"]
  R6 = Resistor [tolerance=±5% resistance=220 package=THT]

nets:
  N1: Part1.RAW, J+GRB.pin1, J-12V.pin2
  GND: Part1.GND, Q3.source, J-12V.pin1, J-IR.pin2, J-DS.pin3, R5.Pin_0, L-RGB.common_cathode, R6.Pin_0
  5V: Part1.VCC, J-IR.pin1, J-DS.pin1, R4.Pin_1, J-LDR.pin1
  N2: Part1.A0, J-LDR.pin2, R5.Pin_1
  N3: Part1.D13/SCK, NRF24L1.SCK
  N4: Part1.D12/MISO, NRF24L1.MISO
  N5: Part1.D11_PWM/MOSI, NRF24L1.MOSI
  N6: Part1.D10_PWM/SS, NRF24L1.CSN
  N7: Part1.D9_PWM, R2.Pin_0
  N8: Part1.D8, NRF24L1.CE
  N9: Part1.D7, L-IR.anode
  N10: Part1.D6_PWM, R3.Pin_0
  N11: Part1.D5_PWM, R1.Pin_0
  N12: Part1.D4, J-IR.pin3
  N13: Part1.D2, J-DS.pin2, R4.Pin_0
  R+: R2.Pin_1, Q2.gate, L-RGB.red_anode
  G+: R1.Pin_1, Q1.gate, L-RGB.blue_anode
  B+: Q3.gate, R3.Pin_1, L-RGB.green_anode
  N14: Q3.drain, J+GRB.pin4
  N15: J+GRB.pin2, Q1.drain
  N16: J+GRB.pin3, Q2.drain
  N17: L-IR.cathode, R6.Pin_1

custom parts:
  NRF24L01: NRF24L01 module
